# Fritzing sketch obstacle avoiding robot (saved by Fritzing 0.9.3b)
circuit board: 8.46667cm x 5.64444cm

parts:
  Part1 = Arduino Uno (Rev3)
  Part3 = Arduino Motor Shield (Rev3)
  U1 = LIPO-2000mAh [package=lipo-2000]
  hc-sr1 = hc-sr04  # not connected
  M1 = Stepper Motor - Bipolar
  M2 = Stepper Motor - Bipolar
  J1 = Basic Servo
  U2 = SWITCH-SPST-2 [package=switch-spst-vertical]
  Part4 = Arduino Motor Shield (Rev3)  # not connected

nets:
  N1: Part1.A0, Part3.A0
  N2: Part1.A1, Part3.A1
  N3: Part1.A2, Part3.A2
  N4: Part1.A3, Part3.A3
  N5: Part1.A4/SDA, Part3.A4, Part3.SDA
  N6: Part1.A5/SCL, Part3.A5, Part3.SCL
  N7: Part1.D8, Part3.D8/BreakeB
  N8: Part1.D9_PWM, Part3.D9/BreakeA, J1.pulse
  N9: Part1.D10_PWM/SS, Part3.D10_PWM
  N10: Part1.D11_PWM/MOSI, Part3.D11_PWM/B
  N11: Part1.D12/MISO, Part3.D12/DirA
  N12: Part1.D13/SCK, Part3.D13/DirB
  GND: Part1.GND, Part3.GND, U1.-, J1.gnd
  N13: Part1.AREF, Part3.AREF
  N14: Part1.D0/RX, Part3.IOREF#118
  N15: Part1.D1/TX, Part3.D1/TX
  N16: Part1.D2, Part3.D2
  N17: Part1.D3_PWM, Part3.D3_PWM/A
  N18: Part1.D4, Part3.D4
  N19: Part1.D5_PWM, Part3.D5_PWM
  N20: Part1.D6_PWM, Part3.D6_PWM
  N21: Part1.D7, Part3.D7
  N22: Part1.ioref, Part3.IOREF#147
  N23: Part1.RESET, Part3.RESET
  3V3: Part1.3V3, Part3.3V3
  5V: Part1.5V, Part3.5V
  VIN: Part1.VIN, Part3.VIN, J1.vcc
  N24: Part3.B-, M1.D
  N25: Part3.B+, M1.B
  N26: Part3.A-, M2.D
  N27: Part3.A+, M2.B
  N28: Part3.VMOT, U2.O
  N29: U1.+, U2.P
